# Fritzing sketch ACC (saved by Fritzing 1.0.6)
breadboards: 1

parts:
  L298N1 = L298N DC motor driver
  U1 = ESP32-38PinWide [part_number=ESP32-38PinWide]
  HC-SR04_Sensor_1 = HC-SR04 Ultrasonic Distance Sensor
  Part1 = InvenSense MPU6050
  VCC2 = Battery [internal_resistance=0.1Ω]
  M1 = gear-motor
  M2 = gear-motor
  M3 = gear-motor
  M4 = gear-motor
  VCC3 = Battery [internal_resistance=0.1Ω]

nets (from the breadboard view):
  N1: L298N1.OUT1, M1.pin_2, M2.pin_2
  N2: L298N1.OUT2, M1.pin_1, M2.pin_1
  N3: L298N1.OUT3, M3.pin_2, M4.pin_2
  N4: L298N1.OUT4, M3.pin_1, M4.pin_1
  N5: L298N1.12V, VCC2.+
  GND: L298N1.GND, U1.GPIO11, HC-SR04_Sensor_1.GND, Part1.GND, VCC2.-, VCC3.-
  N6: L298N1.ENA, U1.GPIO25
  N7: L298N1.ENB, U1.GPIO14
  N8: L298N1.IN1, U1.GPIO26
  N9: L298N1.IN2, U1.GPIO27
  N10: L298N1.IN3, U1.GPIO12
  VCC: U1.3.3, HC-SR04_Sensor_1.VCC, Part1.VCC
  N11: U1.VIN, VCC3.+
  N12: U1.GPIO5, HC-SR04_Sensor_1.TRIG
  N13: U1.GPIO18, HC-SR04_Sensor_1.ECHO
  N14: U1.GPIO21, Part1.SDA
  N15: U1.GPIO22, Part1.SCL

custom parts:
  L298N DC motor driver: 2x DC motor driver with 78M05 positive voltage regulator (7..35 V) L298N: max 46 V, 2 A Set 5 V Enable jumper to enable 5 V regultor (needed for the L298N) and +5 V output at screw terminal or supply external +5 V at screw terminal Set ENA and/or ENB to +5 V to enable motor permanently or supply ENA and/or ENB with PWM signal IN1 and IN2 set rotation directory for motor A (OUT1/OUT2) IN2 and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
  ESP32-38PinWide: Generic 38-Pin ESP32 with wide format (only access to one side of pins on a breadboard) based on Stephen Lilley's HiLetgo ESP-WROOM-32 ESP32 ESP-32S Development Board.
